# Fritzing sketch RthermR1 (saved by Fritzing 0.9.2b)
breadboards: 1

parts:
  R-therm = Temperature Sensor (Thermistor) [thermistor_type=NTC package=THT]
  Vin = DC Power [voltage=5]
  R2 = Resistor [tolerance=±0.5% resistance=220 package=THT]

nets:
  N1: R-therm.pin_0, R2.Pin_1
  N2: R-therm.pin_1, Vin.V+
  N3: Vin.V-, R2.Pin_0
