# Fritzing sketch RthermR2 (saved by Fritzing 0.9.2b)
breadboards: 1

parts:
  R1 = Resistor [tolerance=±0.5% resistance=220 package=THT]
  R-therm = Temperature Sensor (Thermistor) [thermistor_type=NTC package=THT]
  Vin = DC Power [voltage=5]

nets:
  Vout: R1.Pin_0, R-therm.pin_1
  N1: R1.Pin_1, Vin.V+
  N2: R-therm.pin_0, Vin.V-
